# Fritzing sketch DucNguyen_HDC1008 (saved by Fritzing 0.9.3b)
circuit board: 8.46667cm x 5.64444cm
breadboards: 1

parts:
  Screen = Header 4 [package=molex-1x4_lock]
  Sensor = Header 4 [package=molex-1x4_lock]
  HDC1008 = Raspberry Pi 3 [part_number=RPI-3-V1.2]

nets:
  N1: Screen.1, Sensor.4, HDC1008.GND
  N2: Screen.2, Sensor.3, HDC1008.3v3
  N3: Screen.3, Sensor.1, HDC1008.GPIO3
  N4: Screen.4, Sensor.2, HDC1008.GPIO2
